// Logisim project lab2.circ as structural Verilog: 8 circuits, main circuit main
module main (
  input  A,
  input  B,
  input  C
);

  wire seg0_1_s0, seg1_1_s1, seg2_1_s2, seg3_1_s3, seg4_1_s4, seg5_1_s5, seg6_1_s6;

  seg0 seg0_1 (.A(A), .B(B), .C(C), .S0(seg0_1_s0));
  seg1 seg1_1 (.A(A), .B(B), .C(C), .S1(seg1_1_s1));
  seg2 seg2_1 (.A(A), .B(B), .C(C), .S2(seg2_1_s2));
  seg3 seg3_1 (.A(A), .B(B), .C(C), .S3(seg3_1_s3));
  seg4 seg4_1 (.B(B), .C(C), .S4(seg4_1_s4));
  seg5 seg5_1 (.A(A), .B(B), .C(C), .S5(seg5_1_s5));
  seg6 seg6_1 (.A(A), .B(B), .S6(seg6_1_s6));
  _7_Segment_Display u_7_segment_display_1 (
    .g(seg6_1_s6), .f(seg5_1_s5), .a(seg0_1_s0), .b(seg1_1_s1), .e(seg4_1_s4), .d(seg3_1_s3), .c(seg2_1_s2));  // open: dp
endmodule

module seg0 (
  input  A,
  input  B,
  input  C,
  output S0
);

  wire AND1_out, AND2_out, not_1_out, not_2_out;

  not not_1 (not_1_out, A);
  not not_2 (not_2_out, C);
  and AND1 (AND1_out, not_1_out, not_2_out);
  and AND2 (AND2_out, B, not_2_out);
  or OR1 (S0, AND1_out, AND2_out);
endmodule

module seg1 (
  input  A,
  input  B,
  input  C,
  output S1
);

  wire AND1_out, AND2_out, not_1_out, not_2_out, not_3_out;

  not not_1 (not_1_out, A);
  not not_2 (not_2_out, B);
  not not_3 (not_3_out, C);
  and AND1 (AND1_out, not_1_out, not_2_out, C);
  and AND2 (AND2_out, not_1_out, B, not_3_out);
  or OR1 (S1, AND1_out, AND2_out);
endmodule

module seg2 (
  input  A,
  input  B,
  input  C,
  output S2
);

  wire not_1_out, not_2_out, not_3_out, OR1_out, OR2_out;

  not not_1 (not_1_out, A);
  not not_2 (not_2_out, B);
  not not_3 (not_3_out, C);
  or OR1 (OR1_out, A, not_2_out, not_3_out);
  or OR2 (OR2_out, not_1_out, C);
  and AND1 (S2, OR1_out, OR2_out);
endmodule

module seg3 (
  input  A,
  input  B,
  input  C,
  output S3
);

  wire AND1_out, AND2_out, AND3_out, not_1_out, not_2_out, not_3_out;

  not not_1 (not_1_out, A);
  not not_2 (not_2_out, B);
  not not_3 (not_3_out, C);
  and AND1 (AND1_out, A, not_2_out, C);
  and AND2 (AND2_out, not_1_out, not_2_out, not_3_out);
  and AND3 (AND3_out, A, B, not_3_out);
  or OR1 (S3, AND1_out, AND2_out, AND3_out);
endmodule

module seg4 (
  input  B,
  input  C,
  output S4
);

  or OR1 (S4, B, C);
endmodule

module seg5 (
  input  A,
  input  B,
  input  C,
  output S5
);

  wire AND1_out, NOR1_out, not_1_out;

  not not_1 (not_1_out, C);
  nor NOR1 (NOR1_out, A, B);
  and AND1 (AND1_out, B, not_1_out);
  or OR1 (S5, NOR1_out, AND1_out);
endmodule

module seg6 (
  input  A,
  input  B,
  output S6
);

  wire not_1_out;

  not not_1 (not_1_out, A);
  or OR1 (S6, not_1_out, B);
endmodule
