// Logisim project lab3.circ as structural Verilog: 4 circuits, main circuit mux2to1
module mux2to1 (
  input  x,
  input  s,
  input  y,
  output m
);

  wire and_1_out, and_2_out, not_1_out;

  not not_1 (not_1_out, s);
  and and_1 (and_1_out, x, not_1_out);
  and and_2 (and_2_out, s, y);
  or or_1 (m, and_1_out, and_2_out);
endmodule

module demux1to2 (
  input  m,
  input  s,
  output x,
  output y
);

  wire not_1_out;

  not not_1 (not_1_out, s);
  and and_1 (x, m, not_1_out);
  and and_2 (y, s, m);
endmodule

module mux6to1 (
  input  s1,
  input  s2,
  input  s3,
  input  Input0,
  input  Input1,
  input  Input2,
  input  Input3,
  input  Input4,
  input  Input5,
  output Output1
);

  wire mux2to1_1_m, mux2to1_2_m, mux2to1_3_m, mux2to1_4_m;

  mux2to1 mux2to1_1 (.x(Input0), .s(s3), .y(Input1), .m(mux2to1_1_m));
  mux2to1 mux2to1_2 (.x(Input2), .s(s3), .y(Input3), .m(mux2to1_2_m));
  mux2to1 mux2to1_3 (.x(Input4), .s(s3), .y(Input5), .m(mux2to1_3_m));
  mux2to1 mux2to1_4 (.x(mux2to1_1_m), .s(s1), .y(mux2to1_3_m), .m(mux2to1_4_m));
  mux2to1 mux2to1_5 (.x(mux2to1_4_m), .s(s2), .y(mux2to1_2_m), .m(Output1));
endmodule

module demux1to6 (
  input  S3,
  input  S2,
  input  Input1,
  input  S1,
  output Output0,
  output Output1,
  output Output2,
  output Output3,
  output Output4,
  output Output5
);

  wire demux1to2_1_x, demux1to2_1_y, demux1to2_2_x, demux1to2_2_y;

  demux1to2 demux1to2_1 (.m(Input1), .s(S1), .x(demux1to2_1_x), .y(demux1to2_1_y));
  demux1to2 demux1to2_2 (.m(demux1to2_1_x), .s(S2), .x(demux1to2_2_x), .y(demux1to2_2_y));
  demux1to2 demux1to2_3 (.m(demux1to2_2_x), .s(S3), .x(Output0), .y(Output1));
  demux1to2 demux1to2_4 (.m(demux1to2_2_y), .s(S3), .x(Output2), .y(Output3));
  demux1to2 demux1to2_5 (.m(demux1to2_1_y), .s(S3), .x(Output4), .y(Output5));
endmodule
