// Logisim project lab4.circ as structural Verilog: 3 circuits, main circuit main
module main (
  input  S,
  input  Clock,
  input  R,
  output notQ,
  output Q
);

  wire AND1_out, AND2_out;

  and AND1 (AND1_out, S, Clock);
  and AND2 (AND2_out, Clock, R);
  nor NOR1 (notQ, AND1_out, Q);
  nor NOR2 (Q, notQ, AND2_out);
endmodule

module Dflipflop (
  input  D,
  input  C,
  output Q
);

  wire dlatch_1_q, not_1_out;

  not not_1 (not_1_out, C);
  Dlatch dlatch_1 (.D(D), .C(not_1_out), .Q(dlatch_1_q));  // open: notQ
  Dlatch dlatch_2 (.D(dlatch_1_q), .C(C), .Q(Q));  // open: notQ
endmodule

module Dlatch (
  input  D,
  input  C,
  output notQ,
  output Q
);

  wire not_1_out;

  not not_1 (not_1_out, D);
  main main_1 (.S(D), .Clock(C), .R(not_1_out), .notQ(notQ), .Q(Q));
endmodule
