// Logisim project lab6.circ as structural Verilog: 1 circuit, main circuit main
module main (
  input  [3:0] DATA,
  input  CLOCK,
  input  ENABLE,
  input  [1:0] WRITE,
  input  [1:0] READ,
  output [3:0] OUTPUT1
);

  wire demultiplexer_1_out0, demultiplexer_1_out1, demultiplexer_1_out2, demultiplexer_1_out3;
  wire [3:0] R0_q, R1_q, R3_q, register_1_q;

  Demultiplexer #(.enable("false"), .select(2)) demultiplexer_1 (
    .out0(demultiplexer_1_out0), .out1(demultiplexer_1_out1), .out2(demultiplexer_1_out2),
    .out3(demultiplexer_1_out3), .in(ENABLE), .sel(WRITE));
  Register #(.width(4)) R0 (.D(DATA), .en(demultiplexer_1_out0), .clk(CLOCK), .Q(R0_q));  // open: clr
  Register #(.width(4)) R1 (.D(DATA), .en(demultiplexer_1_out1), .clk(CLOCK), .Q(R1_q));  // open: clr
  Register #(.width(4)) register_1 (.D(DATA), .en(demultiplexer_1_out2), .clk(CLOCK), .Q(register_1_q));  // open: clr
  Register #(.width(4)) R3 (.D(DATA), .en(demultiplexer_1_out3), .clk(CLOCK), .Q(R3_q));  // open: clr
  Multiplexer #(.enable("false"), .select(2), .width(4)) multiplexer_1 (
    .in0(R0_q), .in1(R1_q), .in2(register_1_q), .in3(R3_q), .out(OUTPUT1), .sel(READ));
endmodule
